# Fritzing sketch AR05_4digit (saved by Fritzing 0.9.3b)
breadboards: 1

parts:
  R1 = Resistor [tolerance=±5% resistance=330 package=THT]
  R3 = Resistor [tolerance=±5% resistance=330 package=THT]
  R5 = Resistor [tolerance=±5% resistance=330 package=THT]
  R6 = Resistor [tolerance=±5% resistance=330 package=THT]
  R8 = Resistor [tolerance=±5% resistance=330 package=THT]
  부품1 = Arduino Uno (Rev3)
  U1 = 7-SEGMENT-4DIGIT [package=7-segment-4digit-5641]
  R9 = Resistor [tolerance=±5% resistance=330 package=THT]
  R10 = Resistor [tolerance=±5% resistance=330 package=THT]
  R11 = Resistor [tolerance=±5% resistance=330 package=THT]

nets:
  N1: R1.Pin_0, 부품1.D8
  N2: R1.Pin_1, U1.G
  N3: R3.Pin_0, U1.E
  N4: R3.Pin_1, 부품1.D6_PWM
  N5: R5.Pin_0, 부품1.D4
  N6: R5.Pin_1, U1.C
  N7: R6.Pin_0, U1.D
  N8: R6.Pin_1, 부품1.D5_PWM
  N9: R8.Pin_0, 부품1.D9_PWM, U1.DP
  N10: 부품1.D10_PWM/SS, U1.DIG1
  N11: 부품1.D11_PWM/MOSI, U1.DIG2
  N12: 부품1.D12/MISO, U1.DIG3
  N13: 부품1.D13/SCK, U1.DIG4
  N14: 부품1.D2, R9.Pin_1
  N15: 부품1.D3_PWM, R11.Pin_0
  N16: 부품1.D7, R10.Pin_1
  N17: U1.A, R9.Pin_0
  N18: U1.B, R11.Pin_1
  N19: U1.F, R10.Pin_0

custom parts:
  7-SEGMENT-4DIGIT: if you need make parts, send me e-mail and write. Price 1 part=0.9 WMZ (http://www.wmtransfer.com/) ~ 0.9 Euro
