# Fritzing sketch AR05_2led (saved by Fritzing 0.9.3b)
breadboards: 1

parts:
  부품1 = Arduino Uno (Rev3)
  R1 = Resistor [tolerance=±5% resistance=330 package=THT]  # not connected
  LED2 = LED - 5mm [color="Red (633nm)" package="5 mm [THT]"]
  R2 = Resistor [tolerance=±5% resistance=330 package=THT]
  LED1 = smd LED [color="Green (565nm)" package="0603 [SMD]"]

nets:
  N1: 부품1.D3_PWM, LED2.anode
  N2: 부품1.D5_PWM, LED1.anode
  N3: 부품1.GND, R2.Pin_0
  N4: LED2.cathode, R2.Pin_1
