# Fritzing sketch AR05_RGB (saved by Fritzing 0.9.3b)
breadboards: 1

parts:
  부품2 = Arduino Uno (Rev3)
  LED1 = Super Flux RGB LED (com. cathode)

nets:
  N1: 부품2.D3_PWM, LED1.red_anode
  N2: 부품2.D5_PWM, LED1.green_anode
  N3: 부품2.D6_PWM, LED1.blue_anode
  N4: 부품2.GND, LED1.common_cathode
